// Logisim project Adder.circ as structural Verilog
module main (
  input  in_1,
  input  in_2,
  input  in_3,
  output out_4,
  output out_5
);

  wire and_1_out, and_2_out, xor_1_out;

  xor xor_1 (xor_1_out, in_1, in_2);
  and and_1 (and_1_out, in_1, in_2);
  xor xor_2 (out_4, xor_1_out, in_3);
  and and_2 (and_2_out, xor_1_out, in_3);
  or or_1 (out_5, and_2_out, and_1_out);
endmodule

module Half_adder (
  input  in_1,
  input  in_2,
  output out_3,
  output out_4
);

  xor xor_1 (out_3, in_1, in_2);
  and and_1 (out_4, in_2, in_1);
endmodule

module Adder (
  input  in_1,
  input  in_2,
  input  in_3,
  input  in_4,
  input  in_5,
  input  in_6,
  input  in_7,
  input  in_8,
  input  in_9,
  input  in_10,
  input  in_11,
  input  in_12,
  input  in_13,
  input  in_14,
  input  in_15,
  input  in_16,
  output out_17,
  output out_18,
  output out_19,
  output out_20,
  output out_21,
  output out_22,
  output out_23,
  output out_24
);

  wire adder_2_cout, adder_3_cout, adder_4_cout, adder_5_cout, adder_6_cout, adder_7_cout, adder_8_cout;

  Adder_part #(.width(1)) adder_1 (.a(in_1), .b(in_9), .out(out_17), .cin(adder_2_cout));  // open: cout
  Adder_part #(.width(1)) adder_2 (.a(in_2), .b(in_10), .out(out_18), .cin(adder_3_cout), .cout(adder_2_cout));
  Adder_part #(.width(1)) adder_3 (.a(in_3), .b(in_11), .out(out_19), .cin(adder_4_cout), .cout(adder_3_cout));
  Adder_part #(.width(1)) adder_4 (.a(in_4), .b(in_12), .out(out_20), .cin(adder_5_cout), .cout(adder_4_cout));
  Adder_part #(.width(1)) adder_5 (.a(in_5), .b(in_13), .out(out_21), .cin(adder_6_cout), .cout(adder_5_cout));
  Adder_part #(.width(1)) adder_6 (.a(in_6), .b(in_14), .out(out_22), .cin(adder_7_cout), .cout(adder_6_cout));
  Adder_part #(.width(1)) adder_7 (.a(in_7), .b(in_15), .out(out_23), .cin(adder_8_cout), .cout(adder_7_cout));
  Adder_part #(.width(1)) adder_8 (.a(in_8), .b(in_16), .out(out_24), .cout(adder_8_cout));  // open: cin
endmodule
